// Logisim project clock.circ as structural Verilog: 1 circuit, main circuit main
module main (
);

  wire button_1_out, button_2_out, clock_1_out, n7404_1_p5, n7404_1_p6, n7404_1_p8, n7404_2_p2, n7404_2_p4,
       n7404_2_p6, n7404_2_p7, n7408_1_p1, n7408_1_p2, n7408_1_p3, n7408_1_p6, n7408_2_p4, n7408_2_p5,
       n7408_2_p7, n7408_2_p8, n7432_1_p3, n7432_2_p1, n7432_2_p4, n7432_2_p6, n7448_1_p7, n7448_1_p8,
       n7448_1_p9, n7448_1_p10, n7448_1_p11, n7448_1_p12, n7448_1_p13, n7448_2_p7, n7448_2_p8, n7448_2_p9,
       n7448_2_p10, n7448_2_p11, n7448_2_p12, n7448_2_p13, n7448_3_p7, n7448_3_p8, n7448_3_p9, n7448_3_p10,
       n7448_3_p11, n7448_3_p12, n7448_3_p13, n7448_4_p7, n7448_4_p8, n7448_4_p9, n7448_4_p10, n7448_4_p11,
       n7448_4_p12, n7448_4_p13, n74161_1_p1, n74161_1_p2, n74161_1_p4, n74161_1_p5, n74161_1_p6,
       n74161_1_p7, n74161_2_p1, n74161_2_p2, n74161_2_p5, n74161_2_p7, n74161_3_p4, n74161_3_p7,
       n74161_4_p3, n74161_4_p4, n74161_4_p5, n74161_4_p6, n74161_4_p7, n74161_5_p7, n74161_5_p8,
       n74161_5_p9, n74161_5_p10, n74161_6_p4, n74161_6_p6, not_1_out;

  // _74161 74161_1: pin names not known; wires that end beside it: n74161_1_p1, n74161_1_p2, 1'b1, n74161_1_p4, n74161_1_p5, n74161_1_p6, n74161_1_p7, 1'b1, 1'b1
  // _7408 7408_1: pin names not known; wires that end beside it: n7408_1_p1, n7408_1_p2, n7408_1_p3, n7408_1_p3, n74161_1_p5, n7408_1_p6
  // _7448 7448_1: pin names not known; wires that end beside it: n74161_1_p5, n74161_1_p6, 1'b1, 1'b1, n74161_1_p7, n74161_1_p4, n7448_1_p7, n7448_1_p8, n7448_1_p9, n7448_1_p10, n7448_1_p11, n7448_1_p12, n7448_1_p13
  _7_Segment_Display u_7_segment_display_1 (
    .g(n7448_1_p8), .f(n7448_1_p7), .a(n7448_1_p9), .b(n7448_1_p10), .e(n7448_1_p13), .d(n7448_1_p12),
    .c(n7448_1_p11));  // open: dp
  // _7432 7432_1: pin names not known; wires that end beside it: n7408_1_p6, n74161_1_p2, n7432_1_p3
  Button button_1 (.out(button_1_out));
  Button button_2 (.out(button_2_out));
  // _74161 74161_2: pin names not known; wires that end beside it: n74161_2_p1, n74161_2_p2, 1'b1, n7408_1_p2, n74161_2_p5, n7408_1_p1, n74161_2_p7, 1'b1, 1'b1
  // _7432 7432_2: pin names not known; wires that end beside it: n7432_2_p1, button_1_out, n74161_2_p2, n7432_2_p4, button_2_out, n7432_2_p6
  // _7404 7404_1: pin names not known; wires that end beside it: n7408_1_p6, n74161_1_p1, n7432_1_p3, n74161_2_p1, n7404_1_p5, n7404_1_p6, n7432_2_p1, n7404_1_p8
  // _7448 7448_2: pin names not known; wires that end beside it: n74161_2_p5, n7408_1_p1, 1'b1, 1'b1, n74161_2_p7, n7408_1_p2, n7448_2_p7, n7448_2_p8, n7448_2_p9, n7448_2_p10, n7448_2_p11, n7448_2_p12, n7448_2_p13
  _7_Segment_Display u_7_segment_display_2 (
    .g(n7448_2_p8), .f(n7448_2_p7), .a(n7448_2_p9), .b(n7448_2_p10), .e(n7448_2_p13), .d(n7448_2_p12),
    .c(n7448_2_p11));  // open: dp
  // _7408 7408_2: pin names not known; wires that end beside it: n74161_2_p5, n74161_2_p7, n74161_1_p2, n7408_2_p4, n7408_2_p5, n7404_1_p5, n7408_2_p7, n7408_2_p8, n7432_2_p1
  // _74161 74161_3: pin names not known; wires that end beside it: n7404_1_p8, n7404_1_p5, 1'b1, n74161_3_p4, n7408_2_p8, n7408_2_p7, n74161_3_p7, 1'b1, 1'b1
  LED led_1 (.in(clock_1_out));
  LED led_2 (.in(clock_1_out));
  Clock #(.highDuration(1), .lowDuration(1)) clock_1 (.out(clock_1_out));
  not not_1 (not_1_out, n7432_2_p4);
  // _7448 7448_3: pin names not known; wires that end beside it: n7408_2_p8, n7408_2_p7, 1'b1, 1'b1, n74161_3_p7, n74161_3_p4, n7448_3_p7, n7448_3_p8, n7448_3_p9, n7448_3_p10, n7448_3_p11, n7448_3_p12, n7448_3_p13
  // _74161 74161_4: pin names not known; wires that end beside it: not_1_out, clock_1_out, n74161_4_p3, n74161_4_p4, n74161_4_p5, n74161_4_p6, n74161_4_p7
  // _74161 74161_5: pin names not known; wires that end beside it: 1'b1, not_1_out, n74161_4_p3, 1'b1, 1'b1, 1'b1, n74161_5_p7, n74161_5_p8, n74161_5_p9, n74161_5_p10, 1'b1, 1'b1
  _7_Segment_Display u_7_segment_display_3 (
    .g(n7448_3_p8), .f(n7448_3_p7), .a(n7448_3_p9), .b(n7448_3_p10), .e(n7448_3_p13), .d(n7448_3_p12),
    .c(n7448_3_p11));  // open: dp
  // _7404 7404_2: pin names not known; wires that end beside it: n74161_5_p9, n7404_2_p2, n74161_5_p10, n7404_2_p4, n74161_4_p5, n7404_2_p6, n7404_2_p7, n7432_2_p4, n74161_5_p8
  // _74161 74161_6: pin names not known; wires that end beside it: n7404_1_p6, n7432_2_p6, 1'b1, n74161_6_p4, n7408_2_p5, n74161_6_p6, n7408_2_p4, 1'b1, 1'b1
  // _7430 7430_1: pin names not known; wires that end beside it: n74161_4_p4, n7404_2_p6, n74161_4_p6, n74161_4_p7, n74161_5_p7, n7404_2_p4, n7404_2_p2, n7404_2_p7
  // _7448 7448_4: pin names not known; wires that end beside it: n7408_2_p5, n74161_6_p6, 1'b1, 1'b1, n7408_2_p4, n74161_6_p4, n7448_4_p7, n7448_4_p8, n7448_4_p9, n7448_4_p10, n7448_4_p11, n7448_4_p12, n7448_4_p13
  _7_Segment_Display u_7_segment_display_4 (
    .g(n7448_4_p8), .f(n7448_4_p7), .a(n7448_4_p9), .b(n7448_4_p10), .e(n7448_4_p13), .d(n7448_4_p12),
    .c(n7448_4_p11));  // open: dp

  // Notes on the sheet:
  //   74161
  //   7408
  //   7448
  //   7432
  //   74161
  //   H
  //   M
  //   7448
  //   7432
  //   7404
  //   7408
  //   74161
  //   74161
  //   74161
  //   7448
  //   74161
  //   7430
  //   7404
  //   7448
endmodule
